# Fritzing sketch sketch (saved by Fritzing 0.9.3b)
breadboards: 1

parts:
  Часть1 = Arduino Uno (Rev3)
  LED1 = LED - 5mm [color="Green (555nm)" package="5 mm [THT]"]
  LED2 = LED - 5mm [color="Red (633nm)" package="5 mm [THT]"]
  LED3 = LED - 5mm [color="Green (555nm)" package="5 mm [THT]"]
  LED4 = LED - 5mm [color="Red (633nm)" package="5 mm [THT]"]

nets:
  N1: Часть1.D4, LED2.anode
  N2: Часть1.D5_PWM, LED3.anode
  N3: Часть1.D6_PWM, LED4.anode
  N4: Часть1.D7, LED1.anode
  N5: Часть1.GND, LED1.cathode, LED2.cathode, LED3.cathode, LED4.cathode
